// Logisim project cpu.circ as structural Verilog: 1 circuit, main circuit cpu
module cpu (
  input  clk,
  input  [31:0] Instruction,
  input  [31:0] MemReadData,
  output [31:0] MemAddress,
  output [31:0] ProgramCounter,
  output [31:0] ra,
  output [31:0] sp,
  output [31:0] t0,
  output [31:0] t1,
  output [31:0] t2,
  output [31:0] s0,
  output [31:0] s1,
  output [31:0] a0,
  output [3:0] MemWriteMask,
  output [31:0] MemWriteData
);

  wire ASel, BrEq, BrLt, BrUn, BSel, MemEn, PCSel, RegWEn;
  wire [1:0] WBSel;
  wire [2:0] ImmSel;
  wire [3:0] ALUSel;
  wire [31:0] A_Value, B_Value, DataToReg, EXINS_q, EXPC_q, IDINS_q, IDPC_q, immedimate, MAINS_q, MAPC_q,
       PCPlus4, PCValue, ReadData1, ReadData2, register_8_q, register_9_q, WBData, WBINS_q, WBPC_q;

  Register #(.width(32)) PC (.D(PCValue), .clk(clk), .Q(ProgramCounter));  // open: en, clr
  Adder #(.width(32)) adder_1 (.a(ProgramCounter), .b(32'h4), .out(PCPlus4));  // open: cin, cout
  Multiplexer #(.width(32)) multiplexer_1 (.in0(PCPlus4), .in1(MemAddress), .out(PCValue), .sel(PCSel));
  Register #(.width(32)) register_1 (.clk(clk));  // open: D, en, Q, clr
  Register #(.width(32)) register_2 (.clk(clk));  // open: D, en, Q, clr
  Register #(.width(32)) register_3 (.clk(clk));  // open: D, en, Q, clr
  Register #(.width(32)) register_4 (.clk(clk));  // open: D, en, Q, clr
  Register #(.width(32)) register_5 (.clk(clk));  // open: D, en, Q, clr
  Register #(.width(32)) register_6 (.clk(clk));  // open: D, en, Q, clr
  Register #(.width(32)) register_7 ();  // open: D, en, clk, Q, clr
  control_logic control_logic_1 (
    .Instruction(Instruction), .BrEq(BrEq), .BrLt(BrLt), .PCSel(PCSel), .RegWEn(RegWEn), .ImmSel(ImmSel),
    .BrUn(BrUn), .ASel(ASel), .BSel(BSel), .ALUSel(ALUSel), .MemWEn(MemEn), .WBSel(WBSel));
  imm_gen imm_gen_1 (.Instruction(Instruction), .ImmSel(ImmSel), .Immediate(immedimate));
  regfile regfile_1 (
    .ReadIndex1(Instruction[19:15]), .ReadIndex2(Instruction[24:20]), .WriteIndex(Instruction[11:7]),
    .WriteData(WBData), .RegWEn(RegWEn), .clk(clk), .ra(ra), .sp(sp), .t0(t0), .t1(t1), .t2(t2), .s0(s0),
    .s1(s1), .a0(a0), .ReadData1(ReadData1), .ReadData2(ReadData2));
  Register #(.width(32)) IDINS (.D(Instruction), .clk(clk), .Q(IDINS_q));  // open: en, clr
  Register #(.width(32)) IDPC (.D(ProgramCounter), .clk(clk), .Q(IDPC_q));  // open: en, clr
  Register #(.width(32)) register_8 (.D(ReadData1), .clk(clk), .Q(register_8_q));  // open: en, clr
  Register #(.width(32)) register_9 (.D(ReadData2), .clk(clk), .Q(register_9_q));  // open: en, clr
  Register #(.width(32)) EXPC (.D(IDPC_q), .clk(clk), .Q(EXPC_q));  // open: en, clr
  Register #(.width(32)) register_10 (.D(register_8_q), .clk(clk));  // open: en, Q, clr
  Register #(.width(32)) register_11 (.D(register_9_q), .clk(clk));  // open: en, Q, clr
  alu alu_1 (.A(A_Value), .B(B_Value), .ALUSel(ALUSel), .ALUResult(MemAddress));
  branch_comp branch_comp_1 (.BrData1(ReadData1), .BrData2(ReadData2), .BrUn(BrUn), .BrEq(BrEq), .BrLt(BrLt));
  Register #(.width(32)) EXINS (.D(IDINS_q), .clk(clk), .Q(EXINS_q));  // open: en, clr
  Register #(.width(32)) MAINS (.D(EXINS_q), .clk(clk), .Q(MAINS_q));  // open: en, clr
  Register #(.width(32)) MAPC (.D(EXPC_q), .clk(clk), .Q(MAPC_q));  // open: en, clr
  Register #(.width(32)) WBINS (.D(MAINS_q), .clk(clk), .Q(WBINS_q));  // open: en, clr
  Register #(.width(32)) WBPC (.D(MAPC_q), .clk(clk), .Q(WBPC_q));  // open: en, clr
  Multiplexer #(.width(32)) multiplexer_2 (.in0(ReadData2), .in1(immedimate), .out(B_Value), .sel(BSel));
  Multiplexer #(.width(32)) multiplexer_3 (.in0(ReadData1), .in1(ProgramCounter), .out(A_Value), .sel(ASel));
  partial_store partial_store_1 (
    .Instruction(Instruction), .MemAddress(MemAddress), .DataFromReg(ReadData2), .MemWEn(MemEn),
    .MemWriteMask(MemWriteMask), .DataToMem(MemWriteData));
  partial_load partial_load_1 (
    .Instruction(Instruction), .MemAddress(MemAddress), .DataFromMem(MemReadData), .DataToReg(DataToReg));
  Multiplexer #(.select(2), .width(32)) multiplexer_4 (
    .in0(DataToReg), .in1(MemAddress), .in2(PCPlus4), .out(WBData), .sel(WBSel));  // open: in3

  // Other names for the same wires on the sheet: ALUResult[31:0] = MemAddress; rd[4:0] = Instruction[11:7];
  //   rs1[4:0] = Instruction[19:15]; rs2[4:0] = Instruction[24:20]

  // Notes on the sheet:
  //   To IMEM
  //   IMEM (do **NOT** move this)
  //   From IMEM
  //   Inputs/Outputs for testing. Do **NOT** move these.
  //   It is OK to move the PC, RegFile, ALU, MEM, Branch Comp, Imm Gen, Partial Load, Partial Store and Control Logic to wherever is most convenient for you when constructing your CPU, and to delete this text
  //   To DMEM
  //   DMEM (do **NOT** move this)
  //   From DMEM
endmodule
